// Logisim project 1_suma_tres_bits.circ as structural Verilog: 5 circuits, main circuit suma de 3 bits
module suma_de_3_bits (
  input  x0,
  input  x1,
  input  x2,
  input  y0,
  input  y1,
  input  y2,
  output suma0,
  output suma1,
  output suma2,
  output acarreo
);

  wire suma_de_2_bits_1_acarreo;

  suma_de_2_bits suma_de_2_bits_1 (
    .x0(x0), .x1(x1), .y0(y0), .y1(y1), .suma0(suma0), .suma1(suma1), .acarreo(suma_de_2_bits_1_acarreo));
  full_adder_1_bit full_adder_1_bit_1 (
    .x0(x2), .y0(y2), .acarreo0(suma_de_2_bits_1_acarreo), .suma0(suma2), .acarreo0_1(acarreo));

  // Notes on the sheet:
  //   x
  //   y
endmodule

module half_adder_1_bit (
  input  x0,
  input  y0,
  output suma0,
  output acarreo
);

  wire not_1_out, or_1_out;

  or or_1 (or_1_out, x0, y0);
  and and_1 (acarreo, x0, y0);
  not not_1 (not_1_out, acarreo);
  and and_2 (suma0, not_1_out, or_1_out);

  // Notes on the sheet:
  //   x
  //   y
  //   x+y
  //   (xy)
  //   (xy)'(x+y)
endmodule

module full_adder_1_bit (
  input  x0,
  input  y0,
  input  acarreo0,
  output suma0,
  output acarreo0_1
);

  wire half_adder_1_bit_1_acarreo, half_adder_1_bit_1_suma0, half_adder_1_bit_2_acarreo;

  half_adder_1_bit half_adder_1_bit_1 (
    .x0(x0), .y0(y0), .suma0(half_adder_1_bit_1_suma0), .acarreo(half_adder_1_bit_1_acarreo));
  half_adder_1_bit half_adder_1_bit_2 (
    .x0(half_adder_1_bit_1_suma0), .y0(acarreo0), .suma0(suma0), .acarreo(half_adder_1_bit_2_acarreo));
  or or_1 (acarreo0_1, half_adder_1_bit_1_acarreo, half_adder_1_bit_2_acarreo);

  // Notes on the sheet:
  //   x
  //   y
  //   suma x0 y y0
  //   acareo x0 y y0
  //   acareo0
endmodule

module suma_de_2_bits (
  input  x0,
  input  x1,
  input  y0,
  input  y1,
  output suma0,
  output suma1,
  output acarreo
);

  wire half_adder_1_bit_1_acarreo;

  half_adder_1_bit half_adder_1_bit_1 (.x0(x0), .y0(y0), .suma0(suma0), .acarreo(half_adder_1_bit_1_acarreo));
  full_adder_1_bit full_adder_1_bit_1 (
    .x0(x1), .y0(y1), .acarreo0(half_adder_1_bit_1_acarreo), .suma0(suma1), .acarreo0_1(acarreo));

  // Notes on the sheet:
  //   x
  //   y
endmodule

module limpio_pruebas (
  input  x2,
  input  x1,
  input  x0,
  input  y2,
  input  y1,
  input  y0,
  output out_7,
  output out_8,
  output out_9,
  output out_10
);

  suma_de_3_bits suma_de_3_bits_1 (
    .x0(x0), .x1(x1), .x2(x2), .y0(y0), .y1(y1), .y2(y2), .suma0(out_10), .suma1(out_9), .suma2(out_8),
    .acarreo(out_7));

  // Notes on the sheet:
  //   x
  //   +
  //   Resultado
  //   y
endmodule
