// Logisim project 2_elevador.circ as structural Verilog: 1 circuit, main circuit main
module main (
  input  M,
  input  F1,
  input  F2,
  input  F3,
  output salida
);

  wire and_1_out, and_2_out, and_3_out, not_1_out, not_2_out, not_3_out, not_4_out;

  not not_1 (not_1_out, M);
  not not_2 (not_2_out, F1);
  not not_3 (not_3_out, F2);
  not not_4 (not_4_out, F3);
  and and_1 (and_1_out, not_1_out, not_2_out, not_3_out, F3);
  and and_2 (and_2_out, not_1_out, not_2_out, F2, not_4_out);
  and and_3 (and_3_out, not_1_out, F1, not_3_out, not_4_out);
  or or_1 (salida, and_1_out, and_2_out, and_3_out);

  // Notes on the sheet:
  //   M'F1'F2'F3
  //   M'F1'F2F3'
  //   M'F1F2'F3'
endmodule
