// Logisim project 3_circuito_dado.circ as structural Verilog: 1 circuit, main circuit main
module main (
  input  x,
  input  y,
  input  z,
  output xy___y_prime_z
);

  wire and_1_out, and_2_out, not_1_out;

  not not_1 (not_1_out, y);
  and and_1 (and_1_out, x, y);
  and and_2 (and_2_out, not_1_out, z);
  or or_1 (xy___y_prime_z, and_1_out, and_2_out);

  // Notes on the sheet:
  //   xy
  //   y'z
endmodule
