// Logisim project 4_candado version 2.circ as structural Verilog: 1 circuit, main circuit main
module main (
  input  Switch_J,
  input  Switch_L,
  input  Time_Lock_K,
  output JLK___J_prime_L_prime_K
);

  wire and_1_out, and_2_out, not_1_out, not_2_out;

  not not_1 (not_1_out, Switch_J);
  not not_2 (not_2_out, Switch_L);
  and and_1 (and_1_out, Switch_J, Switch_L, Time_Lock_K);
  and and_2 (and_2_out, not_1_out, not_2_out, Time_Lock_K);
  or or_1 (JLK___J_prime_L_prime_K, and_1_out, and_2_out);

  // Notes on the sheet:
  //   JLK
  //   J'L'K
  //   Combination Lock X
endmodule
