// Logisim project 4_candado.circ as structural Verilog: 1 circuit, main circuit main
module main (
  input  Switch_J,
  input  Switch_L,
  input  Time_Lock_K,
  output out_4
);

  and and_1 (out_4, Switch_J, Switch_L, Time_Lock_K);

  // Notes on the sheet:
  //   Combination Lock X
endmodule
