// Logisim project punto extra.circ as structural Verilog: 1 circuit, main circuit main
module main (
  input  x,
  input  y,
  input  z,
  output yz_x
);

  wire yz_out;

  or or_1 (yz_x, x, yz_out);
  and yz (yz_out, y, z);
endmodule
