// Logisim project tarea 1 ED.circ as structural Verilog: 1 circuit, main circuit main
module main (
  input  x,
  input  x_2,
  input  y,
  input  y_2,
  input  z,
  input  z_2,
  input  x_3,
  input  x_4,
  input  y_3,
  input  y_4,
  input  z_3,
  input  z_4,
  output xy___xz___yz,
  output out_14,
  output xy___xz,
  output out_16
);

  wire and_1_out, and_2_out, and_3_out, and_4_out, and_5_out, and_6_out, and_7_out, and_8_out, and_9_out,
       and_10_out, and_11_out, and_12_out, not_1_out, not_2_out, not_3_out, not_4_out, not_5_out;

  not not_1 (not_1_out, x);
  not not_2 (not_2_out, y);
  not not_3 (not_3_out, z);
  not not_4 (not_4_out, y_3);
  not not_5 (not_5_out, z_4);
  and and_1 (and_1_out, x, y, not_3_out);
  and and_2 (and_2_out, x, not_2_out, z);
  and and_3 (and_3_out, not_1_out, y, z);
  and and_4 (and_4_out, x, y, z);
  and and_5 (and_5_out, x_3, y_3, not_5_out);
  and and_6 (and_6_out, x_3, not_4_out, z_4);
  and and_7 (and_7_out, x_3, y_3, z_4);
  or or_1 (out_16, and_5_out, and_6_out, and_7_out);
  or or_2 (out_14, and_1_out, and_2_out, and_3_out, and_4_out);
  and and_8 (and_8_out, x_4, y_4);
  and and_9 (and_9_out, x_4, z_3);
  or or_3 (xy___xz, and_8_out, and_9_out);
  and and_10 (and_10_out, x_2, y_2);
  and and_11 (and_11_out, x_2, z_2);
  and and_12 (and_12_out, y_2, z_2);
  or or_4 (xy___xz___yz, and_10_out, and_11_out, and_12_out);

  // Notes on the sheet:
  //   xyz'
  //   xy'z
  //   xyz
  //   xyz'
  //   xy'z
  //   x'yz
  //   xyz
  //   (xyz')+(xy'z)+(xyz)
  //   (xyz')+(xy'z)+(x'yz)+(xyz)
  //   xy
  //   xz
  //   xy
  //   xz
  //   yz
endmodule
